// Logisim project control_logic.circ as structural Verilog: 1 circuit, main circuit control_logic
module control_logic (
  input  [31:0] inst,
  input  BrEq,
  input  BrLt,
  output PCSel,
  output RegWEn,
  output [2:0] ImmSel,
  output BrUn,
  output ASel,
  output BSel,
  output [3:0] ALUSel,
  output MemRW,
  output [1:0] WBSel
);

  wire add, addi, and_28_out, and_29_out, and_30_out, and_31_out, and_32_out, and_r, andi, auipc, beq, bge,
       bgeu, blt, bltu, bne, bsel_t, comparator_1_eq, comparator_2_eq, comparator_3_eq, comparator_4_eq,
       comparator_5_eq, comparator_6_eq, comparator_7_eq, comparator_8_eq, comparator_9_eq, comparator_10_eq,
       comparator_11_eq, comparator_12_eq, comparator_13_eq, comparator_14_eq, comparator_16_eq,
       comparator_17_eq, comparator_18_eq, comparator_19_eq, comparator_20_eq, comparator_21_eq,
       comparator_22_eq, comparator_23_eq, comparator_24_eq, comparator_25_eq, comparator_27_eq,
       comparator_28_eq, comparator_29_eq, comparator_30_eq, comparator_31_eq, comparator_32_eq,
       comparator_35_eq, comparator_36_eq, comparator_37_eq, comparator_38_eq, comparator_39_eq,
       comparator_40_eq, comparator_41_eq, comparator_42_eq, comparator_43_eq, comparator_44_eq,
       comparator_48_eq, comparator_50_eq, comparator_51_eq, comparator_52_eq, comparator_53_eq,
       comparator_54_eq, comparator_55_eq, divu, I, I_B, jalr, lw3, mul, mulh, mulhu, not_2_out, not_3_out,
       not_4_out, nothing, or_7_out, or_r, ori, R, remu, SB, sll_r, slli, slt, slti, sra_r, srai, srl_r,
       srli, sub, U, xor_r, xori;
  wire [2:0] multiplexer_1_out, multiplexer_2_out, multiplexer_3_out;

  Comparator #(.width(3)) comparator_1 (.a(inst[14:12]), .b(3'b101), .eq(comparator_1_eq));  // open: gt, lt
  Comparator #(.width(7)) comparator_2 (.a(inst[31:25]), .b({7{1'b0}}), .eq(comparator_2_eq));  // open: gt, lt
  Comparator #(.width(3)) comparator_3 (.a(inst[14:12]), .b(3'b000), .eq(comparator_3_eq));  // open: gt, lt
  Comparator #(.width(7)) comparator_4 (.a(inst[31:25]), .b(7'b0000001), .eq(comparator_4_eq));  // open: gt, lt
  Comparator #(.width(3)) comparator_5 (.a(inst[14:12]), .b(3'b000), .eq(comparator_5_eq));  // open: gt, lt
  Comparator #(.width(7)) comparator_6 (.a(inst[31:25]), .b(7'b0100000), .eq(comparator_6_eq));  // open: gt, lt
  Comparator #(.width(3)) comparator_7 (.a(inst[14:12]), .b(3'b000), .eq(comparator_7_eq));  // open: gt, lt
  Comparator #(.width(7)) comparator_8 (.a(inst[31:25]), .b({7{1'b0}}), .eq(comparator_8_eq));  // open: gt, lt
  Comparator #(.width(3)) comparator_9 (.a(inst[14:12]), .b(3'b100), .eq(comparator_9_eq));  // open: gt, lt
  Comparator #(.width(7)) comparator_10 (.a(inst[31:25]), .b(7'b0000001), .eq(comparator_10_eq));  // open: gt, lt
  Comparator #(.width(3)) comparator_11 (.a(inst[14:12]), .b(3'b101), .eq(comparator_11_eq));  // open: gt, lt
  Comparator #(.width(7)) comparator_12 (.a(inst[31:25]), .b({7{1'b0}}), .eq(comparator_12_eq));  // open: gt, lt
  Comparator #(.width(7)) comparator_13 (.a(inst[31:25]), .b({7{1'b0}}), .eq(comparator_13_eq));  // open: gt, lt
  Comparator #(.width(3)) comparator_14 (.a(inst[14:12]), .b(3'b111), .eq(comparator_14_eq));  // open: gt, lt
  Comparator #(.width(7)) comparator_15 (.a(7'b0110111), .b(inst[6:0]), .eq(bsel_t));  // open: gt, lt
  and and_1 (add, comparator_2_eq, comparator_3_eq, R);
  and and_2 (mul, comparator_4_eq, comparator_5_eq, R);
  and and_3 (srl_r, comparator_12_eq, comparator_1_eq, R);
  and and_4 (and_r, comparator_13_eq, comparator_14_eq, R);
  and and_5 (sub, comparator_6_eq, comparator_7_eq, R);
  and and_6 (xor_r, comparator_8_eq, comparator_9_eq, R);
  and and_7 (divu, comparator_10_eq, comparator_11_eq, R);
  or or_1 (RegWEn, R, I, U, WBSel[1]);
  Comparator #(.width(3)) comparator_16 (.a(inst[14:12]), .b(3'b001), .eq(comparator_16_eq));  // open: gt, lt
  Comparator #(.width(3)) comparator_17 (.a(inst[14:12]), .b(3'b001), .eq(comparator_17_eq));  // open: gt, lt
  Comparator #(.width(3)) comparator_18 (.a(inst[14:12]), .b(3'b011), .eq(comparator_18_eq));  // open: gt, lt
  Comparator #(.width(3)) comparator_19 (.a(inst[14:12]), .b(3'b010), .eq(comparator_19_eq));  // open: gt, lt
  Comparator #(.width(3)) comparator_20 (.a(inst[14:12]), .b(3'b101), .eq(comparator_20_eq));  // open: gt, lt
  Comparator #(.width(3)) comparator_21 (.a(inst[14:12]), .b(3'b110), .eq(comparator_21_eq));  // open: gt, lt
  Comparator #(.width(7)) comparator_22 (.a(inst[31:25]), .b(7'b0001111), .eq(comparator_22_eq));  // open: gt, lt
  Comparator #(.width(3)) comparator_23 (.a(inst[14:12]), .b(3'b000), .eq(comparator_23_eq));  // open: gt, lt
  Comparator #(.width(7)) comparator_24 (.a(inst[31:25]), .b(7'b0000001), .eq(comparator_24_eq));  // open: gt, lt
  Comparator #(.width(3)) comparator_25 (.a(inst[14:12]), .b(3'b111), .eq(comparator_25_eq));  // open: gt, lt
  Multiplexer #(.width(3), .enable("false")) multiplexer_1 (
    .in0(3'b000), .in1(3'b001), .out(multiplexer_1_out), .sel(MemRW));
  Comparator #(.width(7)) comparator_26 (.a(inst[6:0]), .b(7'b0110011), .eq(R));  // open: gt, lt
  Comparator #(.width(7)) comparator_27 (.a(inst[31:25]), .b({7{1'b0}}), .eq(comparator_27_eq));  // open: gt, lt
  Comparator #(.width(7)) comparator_28 (.a(inst[31:25]), .b(7'b0000001), .eq(comparator_28_eq));  // open: gt, lt
  Comparator #(.width(7)) comparator_29 (.a(inst[31:25]), .b(7'b0000001), .eq(comparator_29_eq));  // open: gt, lt
  Comparator #(.width(7)) comparator_30 (.a(inst[31:25]), .b({7{1'b0}}), .eq(comparator_30_eq));  // open: gt, lt
  Comparator #(.width(7)) comparator_31 (.a(inst[31:25]), .b(7'b0100000), .eq(comparator_31_eq));  // open: gt, lt
  Comparator #(.width(7)) comparator_32 (.a(inst[31:25]), .b({7{1'b0}}), .eq(comparator_32_eq));  // open: gt, lt
  Multiplexer #(.width(3), .enable("false")) multiplexer_2 (
    .in0(multiplexer_1_out), .in1(3'b010), .out(multiplexer_2_out), .sel(SB));
  and and_8 (sll_r, comparator_27_eq, comparator_16_eq, R);
  and and_9 (mulh, comparator_28_eq, comparator_17_eq, R);
  and and_10 (mulhu, comparator_29_eq, comparator_18_eq, R);
  and and_11 (slt, comparator_30_eq, comparator_19_eq, R);
  and and_12 (sra_r, comparator_31_eq, comparator_20_eq, R);
  and and_13 (or_r, comparator_32_eq, comparator_21_eq, R);
  and and_14 (nothing, comparator_22_eq, comparator_23_eq, R);
  and and_15 (remu, comparator_24_eq, comparator_25_eq, R);
  not not_1 (BSel, R);
  Multiplexer #(.width(3), .enable("false")) multiplexer_3 (
    .in0(multiplexer_2_out), .in1(3'b011), .out(multiplexer_3_out), .sel(U));
  Multiplexer #(.width(3), .enable("false")) multiplexer_4 (
    .in0(multiplexer_3_out), .in1(3'b100), .out(ImmSel), .sel(WBSel[1]));
  Comparator #(.width(7)) comparator_33 (.a(inst[6:0]), .b(7'b0010011), .eq(I_B));  // open: gt, lt
  or or_2 (ASel, SB, auipc, WBSel[1]);
  Comparator #(.width(7)) comparator_34 (.a(inst[6:0]), .b(7'b0000011), .eq(lw3));  // open: gt, lt
  Comparator #(.width(7)) comparator_35 (.a(inst[6:0]), .b(7'b1100111), .eq(comparator_35_eq));  // open: gt, lt
  Comparator #(.width(3)) comparator_36 (.a(inst[14:12]), .b(3'b000), .eq(comparator_36_eq));  // open: gt, lt
  and and_16 (jalr, comparator_35_eq, comparator_36_eq);
  Comparator #(.width(3)) comparator_37 (.a(inst[14:12]), .b(3'b000), .eq(comparator_37_eq));  // open: gt, lt
  Comparator #(.width(3)) comparator_38 (.a(inst[14:12]), .b(3'b001), .eq(comparator_38_eq));  // open: gt, lt
  Comparator #(.width(3)) comparator_39 (.a(inst[14:12]), .b(3'b010), .eq(comparator_39_eq));  // open: gt, lt
  Comparator #(.width(3)) comparator_40 (.a(inst[14:12]), .b(3'b011), .eq(comparator_40_eq));  // open: gt, lt
  or or_3 (I, lw3, I_B, jalr);
  and and_17 (addi, I_B, comparator_37_eq);
  and and_18 (slli, I_B, comparator_38_eq);
  and and_19 (slti, I_B, comparator_39_eq);
  and and_20 (xori, I_B, comparator_40_eq);
  or or_4 (WBSel[0], jalr, lw3);
  or or_5 (BrUn, bltu, bgeu);
  Comparator #(.width(3)) comparator_41 (.a(inst[14:12]), .b(3'b100), .eq(comparator_41_eq));  // open: gt, lt
  Comparator #(.width(3)) comparator_42 (.a(inst[14:12]), .b(3'b101), .eq(comparator_42_eq));  // open: gt, lt
  Comparator #(.width(3)) comparator_43 (.a(inst[14:12]), .b(3'b110), .eq(comparator_43_eq));  // open: gt, lt
  Comparator #(.width(3)) comparator_44 (.a(inst[14:12]), .b(3'b111), .eq(comparator_44_eq));  // open: gt, lt
  Comparator #(.width(7)) comparator_45 (.a(inst[6:0]), .b(7'b0100011), .eq(MemRW));  // open: gt, lt
  Comparator #(.width(7)) comparator_46 (.a(inst[6:0]), .b(7'b1100011), .eq(SB));  // open: gt, lt
  Comparator #(.width(7)) comparator_47 (.a(inst[6:0]), .b(7'b0010111), .eq(auipc));  // open: gt, lt
  Comparator #(.width(7)) comparator_48 (.a(inst[6:0]), .b(7'b0110111), .eq(comparator_48_eq));  // open: gt, lt
  Comparator #(.width(7)) comparator_49 (.a(inst[6:0]), .b(7'b1101111), .eq(WBSel[1]));  // open: gt, lt
  Comparator #(.width(3)) comparator_50 (.a(inst[14:12]), .b(3'b100), .eq(comparator_50_eq));  // open: gt, lt
  and and_21 (srli, I_B, comparator_41_eq);
  and and_22 (srai, I_B, comparator_42_eq);
  and and_23 (ori, I_B, comparator_43_eq);
  and and_24 (andi, I_B, comparator_44_eq);
  or or_6 (U, auipc, comparator_48_eq);
  Comparator #(.width(3)) comparator_51 (.a(inst[14:12]), .b(3'b000), .eq(comparator_51_eq));  // open: gt, lt
  and and_25 (beq, comparator_51_eq, SB);
  Comparator #(.width(3)) comparator_52 (.a(inst[14:12]), .b(3'b001), .eq(comparator_52_eq));  // open: gt, lt
  and and_26 (bne, comparator_52_eq, SB);
  and and_27 (blt, comparator_50_eq, SB);
  not not_2 (not_2_out, BrEq);
  not not_3 (not_3_out, BrLt);
  not not_4 (not_4_out, BrEq);
  or or_7 (or_7_out, bgeu, bge);
  and and_28 (and_28_out, beq, BrEq);
  and and_29 (and_29_out, not_2_out, bne);
  and and_30 (and_30_out, not_3_out, not_4_out, or_7_out);
  and and_31 (and_31_out, blt, BrLt);
  and and_32 (and_32_out, BrLt, bltu);
  or or_8 (PCSel, and_30_out, jalr, WBSel[1], and_28_out, and_29_out, and_31_out, and_32_out);
  Comparator #(.width(3)) comparator_53 (.a(inst[14:12]), .b(3'b101), .eq(comparator_53_eq));  // open: gt, lt
  Comparator #(.width(3)) comparator_54 (.a(inst[14:12]), .b(3'b110), .eq(comparator_54_eq));  // open: gt, lt
  Comparator #(.width(3)) comparator_55 (.a(inst[14:12]), .b(3'b111), .eq(comparator_55_eq));  // open: gt, lt
  and and_33 (bge, comparator_53_eq, SB);
  and and_34 (bltu, comparator_54_eq, SB);
  and and_35 (bgeu, comparator_55_eq, SB);
  or or_9 (ALUSel[2], bsel_t, sll_r);
  or or_10 (ALUSel[1], srl_r, sll_r);
  or or_11 (ALUSel[0], and_r, xor_r);
  or or_12 (ALUSel[3], divu, bsel_t);

  // Other names for the same wires on the sheet: opcode[6:0] = inst[6:0]; imm7_31[24:0] = inst[31:7];
  //   rd[4:0] = inst[11:7]; func3[2:0] = inst[14:12]; rs1[4:0] = inst[19:15]; rs2[4:0] = inst[24:20];
  //   func7[6:0] = inst[31:25]; S = MemRW; UJ = WBSel[1]

  // Notes on the sheet:
  //   INPUTS to your circuit
  //   DON'T CHANGE THE LOCATIONS OF THE INPUTS AND OUTPUTS!
  //   OUTPUT from your circuit
  //   SB type instruction
endmodule
