// Logisim project cpu.circ as structural Verilog: 1 circuit, main circuit main
module main (
  input  [31:0] INSTRUCTION,
  input  CLOCK,
  output [31:0] PROGRAM_COUNTER,
  output [31:0] ra,
  output [31:0] sp,
  output [31:0] t0,
  output [31:0] t1,
  output [31:0] t2,
  output [31:0] s0,
  output [31:0] s1,
  output [31:0] a0
);

  wire BrEq, BrLt, BrUn, RegWEn;
  wire [1:0] WBSel;
  wire [2:0] func3, ImmSel;
  wire [3:0] ALUSel;
  wire [6:0] func7, inst;
  wire [17:0] imm7_31;
  wire [31:0] A, adder_1_out, alu_out, B, dmem_out, immediate, multiplexer_1_out, pc_4, pc_out, wb;

  control_logic control_logic_1 (
    .RegWEn(RegWEn), .ImmSel(ImmSel), .BrUn(BrUn), .BrLt(BrLt), .BrEq(BrEq),
    .inst({func7, imm7_31[17:8], func3, imm7_31[4:0], inst}), .ALUSel(ALUSel), .WBSel(WBSel));  // open: BSel, ASel, PCSel, MemRW
  Adder #(.width(32)) adder_1 (.a(PROGRAM_COUNTER), .b(32'h4), .out(adder_1_out));  // open: cin, cout
  Multiplexer #(.width(32), .enable("false")) multiplexer_1 (
    .in0(adder_1_out), .out(multiplexer_1_out), .sel(1'b0));  // open: in1
  Register #(.width(32)) PC (.D(multiplexer_1_out), .clk(CLOCK), .Q(PROGRAM_COUNTER));  // open: en, clr
  imm_gen imm_gen_1 (.ImmSel(ImmSel), .inst({func7, imm7_31[17:8], func3, imm7_31[4:0], inst}), .imm(immediate));
  Register #(.width(32)) register_1 (.D(PROGRAM_COUNTER), .clk(CLOCK), .Q(pc_out));  // open: en, clr
  Adder #(.width(32)) adder_2 (.a(pc_out), .b(32'h4), .out(pc_4));  // open: cin, cout
  branch_comp branch_comp_1 (.BrEq(BrEq), .BrUn(BrUn), .rs1(A), .BrLt(BrLt), .rs2(B));
  Register #(.width(32)) register_2 (
    .D(INSTRUCTION), .clk(CLOCK), .Q({func7, imm7_31[17:8], func3, imm7_31[4:0], inst}));  // open: en, clr
  regfile_main RegFile (
    .rs2(imm7_31[17:13]), .rd(imm7_31[4:0]), .Read_Data_1(A), .Read_Data_2(B), .ra(ra), .sp(sp), .t0(t0),
    .t1(t1), .t2(t2), .s0(s0), .s1(s1), .a0(a0), .rs1(imm7_31[12:8]), .Write_Data(wb), .RegWEn(RegWEn),
    .clk(CLOCK));
  alu Arithmetic_Logic_Unit (.Result(alu_out), .ALUSel(ALUSel), .B(immediate));  // open: A
  // mem_main DMEM: pin names not known; wires that end beside it: dmem_out
  Multiplexer #(.select(2), .width(32), .enable("false")) multiplexer_2 (
    .in0(alu_out), .in1(pc_4), .in2(dmem_out), .out(wb));  // open: in3, sel

  // Other names for the same wires on the sheet: clk = CLOCK; opcode[6:0] = inst;
  //   inst[31:7] = {func7, imm7_31[17:8], func3, imm7_31[4:0]}; rd[4:0] = imm7_31[4:0];
  //   imm7_31 (some bits) = {func7, func3}; rs1[4:0] = imm7_31[12:8]; rs2[4:0] = imm7_31[17:13]

  // Notes on the sheet:
  //   Output
  //   IMEM (do **NOT** move this)
  //   Inputs
  //   It is OK to move the PC, RegFile, ALU, MEM, Branch Comp, Imm Gen, and Control Logic to wherever is most convenient for you when constructing your CPU, and to delete this text
  //   Inputs/Outputs for testing. Do **NOT** move these.
endmodule
